# Fritzing sketch homebridge-projector (saved by Fritzing 0.9.3b)
breadboards: 1

parts:
  Raspberry_Pi_1 = Raspberry Pi 3 [part_number=RPI-3-V1.2]
  IR1 = TSOP312.., 314.. [package=THT]
  Q1 = TRANSISTOR_NPN [package=to-92]
  R1 = Resistor [tolerance=±5% resistance=220 package=THT]
  R2 = Resistor [tolerance=±5% resistance=220 package="2512 [SMD]"]
  LED1 = LED - 5mm [color="Infrared (940nm)" package="5 mm [THT]"]

nets:
  N1: Raspberry_Pi_1.GIPO22, R2.Pin_0
  N2: Raspberry_Pi_1.GIPO23, IR1.Data
  GND: Raspberry_Pi_1.GND, IR1.GND, LED1.cathode
  N3: Raspberry_Pi_1.5V, IR1.Vs, Q1.C
  N4: Q1.E, R1.Pin_0
  N5: Q1.B, R2.Pin_1
  N6: R1.Pin_1, LED1.anode
